# Fritzing sketch Cerberuino Schematic (saved by Fritzing 0.6.2b)
breadboards: 1

parts:
  Arduino1 = Arduino
  LED1 = RGB LED (com. cathode, rbg) [package="5 mm [THT]"]
  J1 = Piezo Speaker
  S1 = Pushbutton [package=THT]  # not connected
  ANT1 = Antenna  # not connected

nets:
  N1: Arduino1.D7, LED1.red_anode
  N2: Arduino1.D6, LED1.blue_anode
  N3: Arduino1.D5, LED1.green_anode
  N4: Arduino1.D3, J1.pin2
  N5: Arduino1.GND, LED1.common_cathode
